// Logisim project Proj1Circuit.circ as structural Verilog: 1 circuit, main circuit main
module main (
  input  A,
  input  B,
  input  C
);

  wire AB_prime_out, BC_out, or_1_out;

  and AB_prime (AB_prime_out, A, ~B);  // AND_Gate
  and BC (BC_out, B, C);
  or or_1 (or_1_out, AB_prime_out, BC_out);
  LED F (.in(or_1_out));

  // Notes on the sheet:
  //   (AB') + (BC)
endmodule
